// Logisim project parte1_cache.circ as structural Verilog: 1 circuit, main circuit main
module main (
  input  [5:0] Endereco,
  input  [15:0] entradaDados,
  input  in_3,
  input  Clock,
  input  in_5,
  input  in_6,
  input  Resetar
);

  wire and_1_out, counter_1_carry, l0_q, l1_q, l2_q, l3_q, multiplexer_1_out, not_1_out, or_1_out, xor_1_out,
       xor_2_out, xor_3_out;
  wire [3:0] decoder_1_out0, undriven;
  wire [7:0] multiplexer_2_out;
  wire [15:0] Dados_dout;

  D_Flip_Flop l0 (.D(decoder_1_out0[0]), .clk(Clock), .Q(l0_q), .reset(Resetar));  // open: Qn, preset
  D_Flip_Flop l1 (.D(decoder_1_out0[1]), .clk(Clock), .Q(l1_q), .reset(Resetar));  // open: Qn, preset
  D_Flip_Flop l2 (.D(decoder_1_out0[2]), .clk(Clock), .Q(l2_q), .reset(Resetar));  // open: Qn, preset
  D_Flip_Flop l3 (.D(decoder_1_out0[3]), .clk(Clock), .Q(l3_q), .reset(Resetar));  // open: Qn, preset
  Decoder #(.select(2)) decoder_1 (
    .out0(decoder_1_out0[0]), .out1(decoder_1_out0[1]), .out2(decoder_1_out0[2]), .out3(decoder_1_out0[3]),
    .sel(Endereco[2:1]));  // open: en
  Multiplexer #(.select(2)) multiplexer_1 (
    .in0(l0_q), .in1(l1_q), .in2(l2_q), .in3(l3_q), .out(multiplexer_1_out), .sel(Endereco[2:1]));
  LED linha0 (.in(decoder_1_out0[0]));
  LED linha1 (.in(decoder_1_out0[1]));
  LED linha2 (.in(decoder_1_out0[2]));
  LED linha3 (.in(decoder_1_out0[3]));
  RAM #(.addrWidth(2), .dataWidth(3)) TAG (.addr(Endereco[2:1]), .dout({in_3, in_5, in_6}));  // open: we, oe, clk, din
  RAM #(.addrWidth(2), .dataWidth(16)) Dados (
    .addr(Endereco[2:1]), .din(entradaDados), .dout(Dados_dout));  // open: we, oe, clk
  Multiplexer #(.width(8)) multiplexer_2 (
    .in0(Dados_dout[7:0]), .in1(Dados_dout[15:8]), .out(multiplexer_2_out), .sel(Endereco[0]));
  xor xor_1 (xor_1_out, Endereco[3], in_6);
  xor xor_2 (xor_2_out, Endereco[4], in_5);
  xor xor_3 (xor_3_out, Endereco[5], in_3);
  or or_1 (or_1_out, xor_1_out, xor_2_out, xor_3_out);
  not not_1 (not_1_out, or_1_out);
  and and_1 (and_1_out, not_1_out, multiplexer_1_out);
  Counter #(.max('h1), .width(1)) counter_1 (
    .clr(Resetar), .D(and_1_out), .carry(counter_1_carry));  // open: load, up, count, clk, Q
  Hex_Digit_Display hex_digit_display_1 (.value(undriven));  // open: dp

  // Notes on the sheet:
  //   0 - offset
  //   2-1 indice 
  //   5-3 tag
  //   bits validos 0 - 3
  //   TAG enderecamento
  //   T0 - T2
  //   TAG da linha acessada
  //   S0 - S2
  //   2 bytes
  //   offset seleciona um dos 2 bytes de dados
  //   iguais
  //   iguais . valido[indice]
  //   HIT
endmodule
